// Logisim project alu+rf.circ as structural Verilog: 3 circuits, main circuit main
module main (
  input  [7:0] rd,
  input  s,
  input  cin_add,
  input  [2:0] ra,
  input  cin_sub,
  input  [2:0] rb,
  input  we,
  input  [2:0] rw,
  input  [1:0] aluc,
  output [7:0] result,
  output [7:0] qa,
  output z,
  output v,
  output [7:0] qb
);

  wire clock_1_out;
  wire [7:0] multiplexer_1_out;
  wire [31:0] alu_1_clu_out, bit_extender_1_out, bit_extender_2_out;

  Clock clock_1 (.out(clock_1_out));
  Multiplexer #(.width(8), .enable("false")) multiplexer_1 (.in0(rd), .in1(result), .out(multiplexer_1_out), .sel(s));
  in_out in_out_1 (
    .ra(ra), .rb(rb), .rd(multiplexer_1_out), .we(we), .rw(rw), .in_6(clock_1_out), .out_7(qa), .out_8(qb));
  assign bit_extender_1_out = {{24{qa[7]}}, qa};  // Bit_Extender bit_extender_1
  assign bit_extender_2_out = {{24{qb[7]}}, qb};  // Bit_Extender bit_extender_2
  alu alu_1 (
    .cin_add(cin_add), .cin_sub(cin_sub), .A(bit_extender_1_out), .B(bit_extender_2_out), .aluc(aluc), .z(z),
    .v(v), .clu_out(alu_1_clu_out));
  Bit_Extender #(.in_width(32), .out_width(8), .\type ("sign")) bit_extender_3 (.in(alu_1_clu_out), .out(result));
endmodule

module alu (
  input  cin_add,
  input  cin_sub,
  input  [31:0] A,
  input  [31:0] B,
  input  [1:0] aluc,
  output z,
  output v,
  output [31:0] clu_out
);

  wire and_2_out, and_3_out, comparator_1_gt, comparator_1_lt, not_1_out, xnor_1_out, xor_1_out;
  wire [31:0] adder_1_out, and_out, or_out, subtractor_1_out;

  Adder #(.width(32)) adder_1 (.a(A), .b(B), .out(adder_1_out), .cin(cin_add));  // open: cout
  Subtractor #(.width(32)) subtractor_1 (.a(A), .b(B), .out(subtractor_1_out), .bin(cin_sub));  // open: bout
  assign or_out = A | B;  // OR_Gate or, 32 bits wide
  assign and_out = A & B;  // AND_Gate and, 32 bits wide
  not not_1 (not_1_out, A[31]);
  Multiplexer #(.select(2), .width(32), .enable("false")) multiplexer_1 (
    .in0(adder_1_out), .in1(subtractor_1_out), .in2(or_out), .in3(and_out), .out(clu_out), .sel(aluc));
  Comparator #(.width(32)) comparator_1 (
    .a({32{1'b0}}), .b(clu_out), .gt(comparator_1_gt), .eq(z), .lt(comparator_1_lt));
  and and_2 (and_2_out, A[31], comparator_1_lt, xor_1_out);
  xnor xnor_1 (xnor_1_out, B[31], aluc[0]);
  and and_3 (and_3_out, not_1_out, comparator_1_gt, xnor_1_out);
  xor xor_1 (xor_1_out, B[31], aluc[0]);
  or or_2 (v, and_2_out, and_3_out);
endmodule

module in_out (
  input  [2:0] ra,
  input  [2:0] rb,
  input  [7:0] rd,
  input  we,
  input  [2:0] rw,
  input  in_6,
  output [7:0] out_7,
  output [7:0] out_8
);

  wire and_1_out, and_2_out, and_3_out, and_4_out, and_5_out, and_6_out, and_7_out, and_8_out,
       decoder_1_out0, decoder_1_out1, decoder_1_out2, decoder_1_out3, decoder_1_out4, decoder_1_out5,
       decoder_1_out6, decoder_1_out7;
  wire [7:0] register_1_q, register_2_q, register_3_q, register_4_q, register_5_q, register_6_q,
       register_7_q, register_8_q;

  Decoder #(.select(3), .enable("false")) decoder_1 (
    .out0(decoder_1_out0), .out1(decoder_1_out1), .out2(decoder_1_out2), .out3(decoder_1_out3),
    .out4(decoder_1_out4), .out5(decoder_1_out5), .out6(decoder_1_out6), .out7(decoder_1_out7), .sel(rw));
  and and_1 (and_1_out, decoder_1_out0, we);
  and and_2 (and_2_out, decoder_1_out1, we);
  and and_3 (and_3_out, decoder_1_out2, we);
  and and_4 (and_4_out, decoder_1_out3, we);
  and and_5 (and_5_out, decoder_1_out4, we);
  and and_6 (and_6_out, decoder_1_out5, we);
  and and_7 (and_7_out, decoder_1_out6, we);
  and and_8 (and_8_out, decoder_1_out7, we);
  Register register_1 (.D(rd), .en(and_1_out), .Q(register_1_q), .clk(in_6));  // open: clr
  Register register_2 (.D(rd), .en(and_5_out), .Q(register_2_q), .clk(in_6));  // open: clr
  Register register_3 (.D(rd), .en(and_2_out), .Q(register_3_q), .clk(in_6));  // open: clr
  Register register_4 (.D(rd), .en(and_6_out), .Q(register_4_q), .clk(in_6));  // open: clr
  Register register_5 (.D(rd), .en(and_3_out), .Q(register_5_q), .clk(in_6));  // open: clr
  Register register_6 (.D(rd), .en(and_7_out), .Q(register_6_q), .clk(in_6));  // open: clr
  Multiplexer #(.select(3), .width(8)) multiplexer_1 (
    .in0(register_1_q), .in1(register_3_q), .in2(register_5_q), .in3(register_7_q), .in4(register_2_q),
    .in5(register_4_q), .in6(register_6_q), .in7(register_8_q), .out(out_7), .sel(ra));  // open: en
  Register register_7 (.D(rd), .en(and_4_out), .Q(register_7_q), .clk(in_6));  // open: clr
  Register register_8 (.D(rd), .en(and_8_out), .Q(register_8_q), .clk(in_6));  // open: clr
  Multiplexer #(.select(3), .width(8)) multiplexer_2 (
    .in0(register_1_q), .in1(register_3_q), .in2(register_5_q), .in3(register_7_q), .in4(register_2_q),
    .in5(register_4_q), .in6(register_6_q), .in7(register_8_q), .out(out_8), .sel(rb));  // open: en
endmodule
