// Logisim project alu.circ as structural Verilog: 1 circuit, main circuit main
module main (
  input  cin_add,
  input  [31:0] A,
  input  cin_sub,
  input  [31:0] B,
  input  [1:0] aluc,
  output z,
  output v,
  output [31:0] clu_out
);

  wire and_2_out, and_3_out, comparator_1_gt, comparator_1_lt, not_1_out, xnor_1_out, xor_1_out;
  wire [31:0] adder_1_out, and_out, or_out, subtractor_1_out;

  Adder #(.width(32)) adder_1 (.a(A), .b(B), .out(adder_1_out), .cin(cin_add));  // open: cout
  Subtractor #(.width(32)) subtractor_1 (.a(A), .b(B), .out(subtractor_1_out), .bin(cin_sub));  // open: bout
  assign or_out = A | B;  // OR_Gate or, 32 bits wide
  assign and_out = A & B;  // AND_Gate and, 32 bits wide
  not not_1 (not_1_out, A[31]);
  Multiplexer #(.select(2), .width(32), .enable("false")) multiplexer_1 (
    .in0(adder_1_out), .in1(subtractor_1_out), .in2(or_out), .in3(and_out), .out(clu_out), .sel(aluc));
  Comparator #(.width(32)) comparator_1 (
    .a({32{1'b0}}), .b(clu_out), .gt(comparator_1_gt), .eq(z), .lt(comparator_1_lt));
  and and_2 (and_2_out, A[31], comparator_1_lt, xor_1_out);
  xnor xnor_1 (xnor_1_out, B[31], aluc[0]);
  and and_3 (and_3_out, not_1_out, comparator_1_gt, xnor_1_out);
  xor xor_1 (xor_1_out, B[31], aluc[0]);
  or or_2 (v, and_2_out, and_3_out);
endmodule
