// Logisim project cpuX.circ as structural Verilog: 9 circuits, main circuit main
module main (
  input  we,
  input  clk,
  input  clr
);

  wire alu_1_zero, ctrl_1_alusre, ctrl_1_memwrite, ctrl_1_regdst, ctrl_1_regwrite;
  wire [1:0] ctrl_1_extop, ctrl_1_memtoreg, ctrl_1_npcctrol;
  wire [2:0] ctrl_1_aluctr;
  wire [3:0] rf_1_r8, rf_1_r8_2, rf_1_r8_3, rf_1_r8_4, rf_1_r8_5, rf_1_r8_6, rf_1_r8_7, rf_1_r8_8, rf_1_r16,
       rf_1_r16_2, rf_1_r16_3, rf_1_r16_4, rf_1_r16_5, rf_1_r16_6, rf_1_r16_7, rf_1_r16_8, rf_1_r17,
       rf_1_r17_2, rf_1_r17_3, rf_1_r17_4, rf_1_r17_5, rf_1_r17_6, rf_1_r17_7, rf_1_r17_8, rf_1_r18,
       rf_1_r18_2, rf_1_r18_3, rf_1_r18_4, rf_1_r18_5, rf_1_r18_6, rf_1_r18_7, rf_1_r18_8;
  wire [4:0] im_1_rd, im_1_rs, im_1_rt, im_1_sa, multiplexer_1_out;
  wire [5:0] im_1_func, im_1_op;
  wire [15:0] im_1_imm_offset;
  wire [23:0] alu_1_out_5;
  wire [25:0] im_1_adr;
  wire [31:0] dm_1_output, ep_1_eximm, im_1_is, multiplexer_2_out, multiplexer_3_out, npc_1_npc, pc_1_data,
       rf_1_qa, rf_1_qb;
  wire [31:24] alu_1_out_5_2;

  pc pc_1 (.adr(npc_1_npc), .en(we), .clr(clr), .data(pc_1_data), .clk(clk));
  im im_1 (
    .in_adr(pc_1_data[23:0]), .func(im_1_func), .sa(im_1_sa), .rd(im_1_rd), .rt(im_1_rt), .rs(im_1_rs),
    .op(im_1_op), .imm_offset(im_1_imm_offset), .adr(im_1_adr), .is(im_1_is));
  Multiplexer #(.width(5), .enable("false")) multiplexer_1 (
    .in0(im_1_rt), .in1(im_1_rd), .out(multiplexer_1_out), .sel(ctrl_1_regdst));
  ctrl ctrl_1 (
    .ALUSre(ctrl_1_alusre), .RegDst(ctrl_1_regdst), .MemWrite(ctrl_1_memwrite), .ALUctr(ctrl_1_aluctr),
    .zero(alu_1_zero), .op(im_1_op), .func(im_1_func), .npcctrol(ctrl_1_npcctrol), .Extop(ctrl_1_extop),
    .MemToReg(ctrl_1_memtoreg), .RegWrite(ctrl_1_regwrite));
  ep ep_1 (.imm(im_1_imm_offset), .extop(ctrl_1_extop), .eximm(ep_1_eximm));
  rf rf_1 (
    .clr(clr), .rw(multiplexer_1_out), .clk(clk), .data(multiplexer_3_out), .we(ctrl_1_regwrite),
    .r16({rf_1_r16_8, rf_1_r16_7, rf_1_r16_6, rf_1_r16_5, rf_1_r16_4, rf_1_r16_3, rf_1_r16_2, rf_1_r16}),
    .r17({rf_1_r17_8, rf_1_r17_7, rf_1_r17_6, rf_1_r17_5, rf_1_r17_4, rf_1_r17_3, rf_1_r17_2, rf_1_r17}),
    .r18({rf_1_r18_8, rf_1_r18_7, rf_1_r18_6, rf_1_r18_5, rf_1_r18_4, rf_1_r18_3, rf_1_r18_2, rf_1_r18}),
    .r8({rf_1_r8_8, rf_1_r8_7, rf_1_r8_6, rf_1_r8_5, rf_1_r8_4, rf_1_r8_3, rf_1_r8_2, rf_1_r8}),
    .qb(rf_1_qb), .rb(im_1_rt), .qa(rf_1_qa), .ra(im_1_rs));
  Multiplexer #(.width(32), .enable("false")) multiplexer_2 (
    .in0(rf_1_qb), .in1(ep_1_eximm), .out(multiplexer_2_out), .sel(ctrl_1_alusre));
  npc npc_1 (.pc(pc_1_data), .addr(im_1_adr), .offest(im_1_imm_offset), .npc(npc_1_npc), .npcctrol(ctrl_1_npcctrol));
  alu alu_1 (
    .aluc(ctrl_1_aluctr), .in_2(rf_1_qa), .B(multiplexer_2_out), .Zero(alu_1_zero),
    .out_5({alu_1_out_5_2, alu_1_out_5}));
  Multiplexer #(.select(2), .width(32), .enable("false")) multiplexer_3 (
    .in0({alu_1_out_5_2, alu_1_out_5}), .in1(dm_1_output), .in2(ep_1_eximm), .out(multiplexer_3_out),
    .sel(ctrl_1_memtoreg));  // open: in3
  dm dm_1 (
    .address(alu_1_out_5), .\input (rf_1_qb), .we(ctrl_1_memwrite), .clk(clk), .clr(clr),
    .\output (dm_1_output));
  Hex_Digit_Display hex_digit_display_1 (.value(rf_1_r8_8));  // open: dp
  Hex_Digit_Display hex_digit_display_2 (.value(rf_1_r8_7));  // open: dp
  Hex_Digit_Display hex_digit_display_3 (.value(rf_1_r16_8));  // open: dp
  Hex_Digit_Display hex_digit_display_4 (.value(rf_1_r16_7));  // open: dp
  Hex_Digit_Display hex_digit_display_5 (.value(rf_1_r17_8));  // open: dp
  Hex_Digit_Display hex_digit_display_6 (.value(rf_1_r17_7));  // open: dp
  Hex_Digit_Display hex_digit_display_7 (.value(rf_1_r18_8));  // open: dp
  Hex_Digit_Display hex_digit_display_8 (.value(rf_1_r18_7));  // open: dp
  Hex_Digit_Display hex_digit_display_9 (.value(im_1_is[27:24]));  // open: dp
  Hex_Digit_Display hex_digit_display_10 (.value(im_1_is[31:28]));  // open: dp
  Hex_Digit_Display hex_digit_display_11 (.value(dm_1_output[31:28]));  // open: dp
  Hex_Digit_Display hex_digit_display_12 (.value(dm_1_output[27:24]));  // open: dp
  Hex_Digit_Display hex_digit_display_13 (.value(rf_1_r8_5));  // open: dp
  Hex_Digit_Display hex_digit_display_14 (.value(rf_1_r8_6));  // open: dp
  Hex_Digit_Display hex_digit_display_15 (.value(rf_1_r16_6));  // open: dp
  Hex_Digit_Display hex_digit_display_16 (.value(rf_1_r16_5));  // open: dp
  Hex_Digit_Display hex_digit_display_17 (.value(rf_1_r17_6));  // open: dp
  Hex_Digit_Display hex_digit_display_18 (.value(rf_1_r17_5));  // open: dp
  Hex_Digit_Display hex_digit_display_19 (.value(rf_1_r18_6));  // open: dp
  Hex_Digit_Display hex_digit_display_20 (.value(rf_1_r18_5));  // open: dp
  Hex_Digit_Display hex_digit_display_21 (.value(im_1_is[19:16]));  // open: dp
  Hex_Digit_Display hex_digit_display_22 (.value(im_1_is[23:20]));  // open: dp
  Hex_Digit_Display hex_digit_display_23 (.value(dm_1_output[19:16]));  // open: dp
  Hex_Digit_Display hex_digit_display_24 (.value(dm_1_output[23:20]));  // open: dp
  Hex_Digit_Display hex_digit_display_25 (.value(rf_1_r8_4));  // open: dp
  Hex_Digit_Display hex_digit_display_26 (.value(rf_1_r8_3));  // open: dp
  Hex_Digit_Display hex_digit_display_27 (.value(rf_1_r16_4));  // open: dp
  Hex_Digit_Display hex_digit_display_28 (.value(rf_1_r16_3));  // open: dp
  Hex_Digit_Display hex_digit_display_29 (.value(rf_1_r17_4));  // open: dp
  Hex_Digit_Display hex_digit_display_30 (.value(rf_1_r17_3));  // open: dp
  Hex_Digit_Display hex_digit_display_31 (.value(rf_1_r18_3));  // open: dp
  Hex_Digit_Display hex_digit_display_32 (.value(rf_1_r18_4));  // open: dp
  Hex_Digit_Display hex_digit_display_33 (.value(im_1_is[15:12]));  // open: dp
  Hex_Digit_Display hex_digit_display_34 (.value(im_1_is[11:8]));  // open: dp
  Hex_Digit_Display hex_digit_display_35 (.value(dm_1_output[15:12]));  // open: dp
  Hex_Digit_Display hex_digit_display_36 (.value(dm_1_output[11:8]));  // open: dp
  Hex_Digit_Display hex_digit_display_37 (.value(rf_1_r8));  // open: dp
  Hex_Digit_Display hex_digit_display_38 (.value(rf_1_r8_2));  // open: dp
  Hex_Digit_Display hex_digit_display_39 (.value(rf_1_r16_2));  // open: dp
  Hex_Digit_Display hex_digit_display_40 (.value(rf_1_r16));  // open: dp
  Hex_Digit_Display hex_digit_display_41 (.value(rf_1_r17));  // open: dp
  Hex_Digit_Display hex_digit_display_42 (.value(rf_1_r17_2));  // open: dp
  Hex_Digit_Display hex_digit_display_43 (.value(rf_1_r18));  // open: dp
  Hex_Digit_Display hex_digit_display_44 (.value(rf_1_r18_2));  // open: dp
  Hex_Digit_Display hex_digit_display_45 (.value(im_1_is[3:0]));  // open: dp
  Hex_Digit_Display hex_digit_display_46 (.value(im_1_is[7:4]));  // open: dp
  Hex_Digit_Display hex_digit_display_47 (.value(dm_1_output[7:4]));  // open: dp
  Hex_Digit_Display hex_digit_display_48 (.value(dm_1_output[3:0]));  // open: dp

  // Notes on the sheet:
  //   MUX15
  //   MUX132
  //   MUX232
  //   R8
  //   R16
  //   R17
  //   R18
  //   IR
endmodule

module alu (
  input  [2:0] aluc,
  input  [31:0] in_2,
  input  [31:0] B,
  output Zero,
  output [31:0] out_5
);

  wire comparator_1_lt, not_1_out;
  wire [31:0] adder_1_out, and_1_out, bit_extender_1_out, or_1_out, subtractor_1_out;

  Adder #(.width(32)) adder_1 (.a(in_2), .b(B), .out(adder_1_out));  // open: cin, cout
  Subtractor #(.width(32)) subtractor_1 (.a(in_2), .b(B), .out(subtractor_1_out));  // open: bin, bout
  assign or_1_out = in_2 | B;  // OR_Gate or_1, 32 bits wide
  assign and_1_out = in_2 & B;  // AND_Gate and_1, 32 bits wide
  Comparator #(.width(32)) comparator_1 (.a(B), .b(in_2), .lt(comparator_1_lt));  // open: gt, eq
  not not_1 (not_1_out, comparator_1_lt);
  assign bit_extender_1_out = {{31{1'b0}}, not_1_out};  // Bit_Extender bit_extender_1
  Multiplexer #(.select(3), .width(32), .enable("false")) multiplexer_1 (
    .in0(adder_1_out), .in1(and_1_out), .in2(or_1_out), .in4(subtractor_1_out), .in7(bit_extender_1_out),
    .out(out_5), .sel(aluc));  // open: in3, in5, in6
  Comparator #(.width(32)) comparator_2 (.a({32{1'b0}}), .b(out_5), .eq(Zero));  // open: gt, lt

  // Notes on the sheet:
  //   A
  //   COMP
  //   COMP
  //   alu_out
endmodule

module rf (
  input  clr,
  input  [4:0] rw,
  input  [4:0] rb,
  input  clk,
  input  [31:0] data,
  input  [4:0] ra,
  input  we,
  output [31:0] qb,
  output [31:0] qa,
  output [31:0] r16,
  output [31:0] r17,
  output [31:0] r18,
  output [31:0] r8
);

  wire and_1_out, and_2_out, and_3_out, and_4_out, and_5_out, and_6_out, and_7_out, and_8_out, and_9_out,
       and_10_out, and_11_out, and_12_out, and_13_out, and_14_out, and_15_out, and_16_out, and_17_out,
       and_18_out, and_19_out, and_20_out, and_21_out, and_22_out, and_23_out, and_24_out, and_25_out,
       and_26_out, and_27_out, and_28_out, and_29_out, and_30_out, and_31_out, and_32_out, decoder_1_out0,
       decoder_1_out1, decoder_1_out2, decoder_1_out3, decoder_1_out4, decoder_1_out5, decoder_1_out6,
       decoder_1_out7, decoder_1_out8, decoder_1_out9, decoder_1_out10, decoder_1_out11, decoder_1_out12,
       decoder_1_out13, decoder_1_out14, decoder_1_out15, decoder_1_out16, decoder_1_out17, decoder_1_out18,
       decoder_1_out19, decoder_1_out20, decoder_1_out21, decoder_1_out22, decoder_1_out23, decoder_1_out24,
       decoder_1_out25, decoder_1_out26, decoder_1_out27, decoder_1_out28, decoder_1_out29, decoder_1_out30,
       decoder_1_out31;
  wire [31:0] r0_q, r1_q, r2_q, r3_q, r4_q, r5_q, r6_q, r7_q, r9_q, r10_q, r11_q, r12_q, r13_q, r14_q, r15_q,
       r19_q, r20_q, r21_q, r22_q, r23_q, r24_q, r25_q, r26_q, r27_q, r28_q, r29_q, r30_q, r31_q;

  Decoder #(.select(5), .enable("false")) decoder_1 (
    .out0(decoder_1_out0), .out1(decoder_1_out1), .out2(decoder_1_out2), .out3(decoder_1_out3),
    .out4(decoder_1_out4), .out5(decoder_1_out5), .out6(decoder_1_out6), .out7(decoder_1_out7),
    .out8(decoder_1_out8), .out9(decoder_1_out9), .out10(decoder_1_out10), .out11(decoder_1_out11),
    .out12(decoder_1_out12), .out13(decoder_1_out13), .out14(decoder_1_out14), .out15(decoder_1_out15),
    .out16(decoder_1_out16), .out17(decoder_1_out17), .out18(decoder_1_out18), .out19(decoder_1_out19),
    .out20(decoder_1_out20), .out21(decoder_1_out21), .out22(decoder_1_out22), .out23(decoder_1_out23),
    .out24(decoder_1_out24), .out25(decoder_1_out25), .out26(decoder_1_out26), .out27(decoder_1_out27),
    .out28(decoder_1_out28), .out29(decoder_1_out29), .out30(decoder_1_out30), .out31(decoder_1_out31),
    .sel(rw));
  and and_1 (and_1_out, decoder_1_out16, we);
  and and_2 (and_2_out, decoder_1_out17, we);
  and and_3 (and_3_out, decoder_1_out18, we);
  and and_4 (and_4_out, decoder_1_out19, we);
  and and_5 (and_5_out, decoder_1_out20, we);
  and and_6 (and_6_out, decoder_1_out21, we);
  and and_7 (and_7_out, decoder_1_out22, we);
  and and_8 (and_8_out, decoder_1_out23, we);
  and and_9 (and_9_out, decoder_1_out24, we);
  and and_10 (and_10_out, decoder_1_out25, we);
  and and_11 (and_11_out, decoder_1_out26, we);
  and and_12 (and_12_out, decoder_1_out27, we);
  and and_13 (and_13_out, decoder_1_out28, we);
  and and_14 (and_14_out, decoder_1_out29, we);
  and and_15 (and_15_out, decoder_1_out30, we);
  and and_16 (and_16_out, decoder_1_out31, we);
  and and_17 (and_17_out, decoder_1_out0, we);
  and and_18 (and_18_out, decoder_1_out1, we);
  buf and_19 (and_19_out, decoder_1_out2);  // AND_Gate
  and and_20 (and_20_out, decoder_1_out3, we);
  and and_21 (and_21_out, decoder_1_out4, we);
  and and_22 (and_22_out, decoder_1_out5, we);
  and and_23 (and_23_out, decoder_1_out6, we);
  and and_24 (and_24_out, decoder_1_out7, we);
  and and_25 (and_25_out, decoder_1_out8, we);
  and and_26 (and_26_out, decoder_1_out9, we);
  and and_27 (and_27_out, decoder_1_out10, we);
  and and_28 (and_28_out, decoder_1_out11, we);
  and and_29 (and_29_out, decoder_1_out12, we);
  and and_30 (and_30_out, decoder_1_out13, we);
  and and_31 (and_31_out, decoder_1_out14, we);
  and and_32 (and_32_out, decoder_1_out15, we);
  Register #(.width(32)) r0 (.D(data), .en(and_17_out), .Q(r0_q), .clk(clk), .clr(clr));
  Register #(.width(32)) r4 (.D(data), .en(and_21_out), .Q(r4_q), .clk(clk), .clr(clr));
  Register #(.width(32)) u_r8 (.D(data), .en(and_25_out), .Q(r8), .clk(clk), .clr(clr));
  Register #(.width(32)) r12 (.D(data), .en(and_29_out), .Q(r12_q), .clk(clk), .clr(clr));
  Register #(.width(32)) u_r16 (.D(data), .en(and_1_out), .Q(r16), .clk(clk), .clr(clr));
  Register #(.width(32)) r20 (.D(data), .en(and_5_out), .Q(r20_q), .clk(clk), .clr(clr));
  Register #(.width(32)) r24 (.en(and_9_out), .Q(r24_q), .clk(clk), .clr(clr));  // open: D
  Register #(.width(32)) r28 (.D(data), .en(and_13_out), .Q(r28_q), .clk(clk), .clr(clr));
  Register #(.width(32)) r1 (.D(data), .en(and_18_out), .Q(r1_q), .clk(clk), .clr(clr));
  Register #(.width(32)) r5 (.D(data), .en(and_22_out), .Q(r5_q), .clk(clk), .clr(clr));
  Register #(.width(32)) r9 (.D(data), .en(and_26_out), .Q(r9_q), .clk(clk), .clr(clr));
  Register #(.width(32)) r13 (.D(data), .en(and_30_out), .Q(r13_q), .clk(clk), .clr(clr));
  Register #(.width(32)) u_r17 (.D(data), .en(and_2_out), .Q(r17), .clk(clk), .clr(clr));
  Register #(.width(32)) r21 (.D(data), .en(and_6_out), .Q(r21_q), .clk(clk), .clr(clr));
  Register #(.width(32)) r25 (.en(and_10_out), .Q(r25_q), .clk(clk), .clr(clr));  // open: D
  Register #(.width(32)) r29 (.D(data), .en(and_14_out), .Q(r29_q), .clk(clk), .clr(clr));
  Register #(.width(32)) r2 (.D(data), .en(and_19_out), .Q(r2_q), .clk(clk), .clr(clr));
  Register #(.width(32)) r6 (.D(data), .en(and_23_out), .Q(r6_q), .clk(clk), .clr(clr));
  Register #(.width(32)) r10 (.D(data), .en(and_27_out), .Q(r10_q), .clk(clk), .clr(clr));
  Register #(.width(32)) r14 (.D(data), .en(and_31_out), .Q(r14_q), .clk(clk), .clr(clr));
  Register #(.width(32)) u_r18 (.D(data), .en(and_3_out), .Q(r18), .clk(clk), .clr(clr));
  Register #(.width(32)) r22 (.D(data), .en(and_7_out), .Q(r22_q), .clk(clk), .clr(clr));
  Register #(.width(32)) r26 (.en(and_11_out), .Q(r26_q), .clk(clk), .clr(clr));  // open: D
  Register #(.width(32)) r30 (.D(data), .en(and_15_out), .Q(r30_q), .clk(clk), .clr(clr));
  Register #(.width(32)) r3 (.D(data), .en(and_20_out), .Q(r3_q), .clk(clk), .clr(clr));
  Register #(.width(32)) r7 (.D(data), .en(and_24_out), .Q(r7_q), .clk(clk), .clr(clr));
  Register #(.width(32)) r11 (.D(data), .en(and_28_out), .Q(r11_q), .clk(clk), .clr(clr));
  Register #(.width(32)) r15 (.D(data), .en(and_32_out), .Q(r15_q), .clk(clk), .clr(clr));
  Register #(.width(32)) r19 (.D(data), .en(and_4_out), .Q(r19_q), .clk(clk), .clr(clr));
  Register #(.width(32)) r23 (.D(data), .en(and_8_out), .Q(r23_q), .clk(clk), .clr(clr));
  Register #(.width(32)) r27 (.en(and_12_out), .Q(r27_q), .clk(clk), .clr(clr));  // open: D
  Register #(.width(32)) r31 (.D(data), .en(and_16_out), .Q(r31_q), .clk(clk), .clr(clr));
  Multiplexer #(.select(5), .width(32)) multiplexer_1 (
    .in0(r0_q), .in1(r1_q), .in2(r2_q), .in3(r3_q), .in4(r4_q), .in5(r5_q), .in6(r6_q), .in7(r7_q), .in8(r8),
    .in9(r9_q), .in10(r10_q), .in11(r11_q), .in12(r12_q), .in13(r13_q), .in14(r14_q), .in15(r15_q),
    .in16(r16), .in17(r17), .in18(r18), .in19(r19_q), .in20(r20_q), .in21(r21_q), .in22(r22_q), .in23(r23_q),
    .in24(r24_q), .in25(r25_q), .in26(r26_q), .in27(r27_q), .in28(r28_q), .in29(r29_q), .in30(r30_q),
    .in31(r31_q), .out(qb), .sel(rb));  // open: en
  Multiplexer #(.select(5), .width(32)) multiplexer_2 (
    .in0(r0_q), .in1(r1_q), .in2(r2_q), .in3(r3_q), .in4(r4_q), .in5(r5_q), .in6(r6_q), .in7(r7_q), .in8(r8),
    .in9(r9_q), .in10(r10_q), .in11(r11_q), .in12(r12_q), .in13(r13_q), .in14(r14_q), .in15(r15_q),
    .in16(r16), .in17(r17), .in18(r18), .in19(r19_q), .in20(r20_q), .in21(r21_q), .in22(r22_q), .in23(r23_q),
    .in24(r24_q), .in25(r25_q), .in26(r26_q), .in27(r27_q), .in28(r28_q), .in29(r29_q), .in30(r30_q),
    .in31(r31_q), .out(qa), .sel(ra));  // open: en

  // Notes on the sheet:
  //   mux_b
  //   mux_a
endmodule

module pc (
  input  [31:0] adr,
  input  en,
  input  clk,
  input  clr,
  output [31:0] data
);

  Register #(.width(32)) register_1 (.D(adr), .en(en), .Q(data), .clk(clk), .clr(clr));
endmodule

module im (
  input  [23:0] in_adr,
  output [5:0] func,
  output [4:0] sa,
  output [4:0] rd,
  output [4:0] rt,
  output [4:0] rs,
  output [5:0] op,
  output [15:0] imm_offset,
  output [25:0] adr,
  output [31:0] is
);

  ROM #(.addrWidth(24), .dataWidth(32)) rom_1 (.addr(in_adr), .data({is[31:26], adr}));  // open: sel

  assign func = adr[5:0];
  assign imm_offset = adr[15:0];
  assign is[25:0] = adr;
  assign op = is[31:26];
  assign rd = adr[15:11];
  assign rs = adr[25:21];
  assign rt = adr[20:16];
  assign sa = adr[10:6];

  // Notes on the sheet:
  //   contents of rom_1 (hex, n*v repeats v):
  //   20100003 0 0 0 20110004 0 0 0 211402a 0 0 0 2008000a 0 0 0 12280004 0 0 0 2129020 0 0 0 22100001 0 0
  //   0 22310001 0 0 0 8000004 0 0 0 ac120040 0 0 0 8c100040
endmodule

module ep (
  input  [15:0] imm,
  input  [1:0] extop,
  output [31:0] eximm
);

  wire [31:0] bit_extender_1_out, bit_extender_2_out;

  assign bit_extender_1_out = {{16{1'b0}}, imm};  // Bit_Extender bit_extender_1
  assign bit_extender_2_out = {{16{imm[15]}}, imm};  // Bit_Extender bit_extender_2
  Multiplexer #(.select(2), .width(32)) multiplexer_1 (
    .in0(bit_extender_1_out), .in1(bit_extender_2_out), .in2({imm, {16{1'b0}}}), .out(eximm), .sel(extop));  // open: in3, en
endmodule

module ctrl (
  input  [5:0] func,
  input  [5:0] op,
  input  zero,
  output RegWrite,
  output ALUSre,
  output RegDst,
  output [1:0] MemToReg,
  output MemWrite,
  output [1:0] npcctrol,
  output [1:0] Extop,
  output [2:0] ALUctr
);

  wire addi_out, and_2_out, and_3_out, and_4_out, and_5_out;
  wire [2:0] or_4_out;
  wire [2:1] ori_out;

  and R_type (RegDst, ~op[5], ~op[4], ~op[3], ~op[2], ~op[1], ~op[0]);  // AND_Gate
  and ori (ori_out[1], ~op[5], ~op[4], op[3], op[2], ~op[1], op[0]);  // AND_Gate
  and lw (MemToReg[0], op[5], ~op[4], ~op[3], ~op[2], op[1], op[0]);  // AND_Gate
  and sw (MemWrite, op[5], ~op[4], op[3], ~op[2], op[1], op[0]);  // AND_Gate
  and beq (ori_out[2], ~op[5], ~op[4], ~op[3], op[2], ~op[1], ~op[0]);  // AND_Gate
  and jump (npcctrol[0], ~op[5], ~op[4], ~op[3], ~op[2], op[1], ~op[0]);  // AND_Gate
  and lui (Extop[1], ~op[5], ~op[4], op[3], op[2], op[1], op[0]);  // AND_Gate
  and addi (addi_out, ~op[5], ~op[4], op[3], ~op[2], ~op[1], ~op[0]);  // AND_Gate
  and and_1 (npcctrol[1], ori_out[2], zero);
  or or_1 (Extop[0], MemToReg[0], MemWrite);
  or or_2 (RegWrite, Extop[1], addi_out, RegDst, ori_out[1], MemToReg[0]);
  or or_3 (ALUSre, addi_out, ori_out[1], MemToReg[0], MemWrite);
  and and_2 (and_2_out, ~func[3], func[2], ~func[1], ~func[0]);  // AND_Gate
  and and_3 (and_3_out, func[3], ~func[2], func[1], ~func[0]);  // AND_Gate
  and and_4 (and_4_out, ~func[3], func[2], ~func[1], func[0]);  // AND_Gate
  Multiplexer #(.width(3)) multiplexer_1 (
    .in0({ori_out, RegDst}), .in1(or_4_out), .out(ALUctr), .sel(RegDst));  // open: en
  and and_5 (and_5_out, func[3], ~func[2], func[1], ~func[0]);  // AND_Gate
  and and_6 (or_4_out[2], ~func[2], func[1], ~func[0]);  // AND_Gate
  or or_4 (or_4_out[0], and_2_out, and_3_out);
  or or_5 (or_4_out[1], and_4_out, and_5_out);

  assign MemToReg[1] = Extop[1];
endmodule

module dm (
  input  [23:0] address,
  input  [31:0] \input ,
  input  we,
  input  clk,
  input  clr,
  output [31:0] \output 
);

  RAM #(.addrWidth(24), .dataWidth(32), .bus("separate")) ram_1 (
    .addr(address), .din(\input ), .data(\output ), .str(we), .clk(clk), .clr(clr));  // open: sel, ld
endmodule

module npc (
  input  [1:0] npcctrol,
  input  [31:0] pc,
  input  [25:0] addr,
  input  [15:0] offest,
  output [31:0] npc
);

  wire [31:0] adder_1_out, adder_2_out, bit_extender_1_out, shifter_1_out;

  assign bit_extender_1_out = {{16{offest[15]}}, offest};  // Bit_Extender bit_extender_1
  Adder #(.width(32)) adder_1 (.a(32'h4), .b(pc), .out(adder_1_out));  // open: cin, cout
  Shifter #(.width(32)) shifter_1 (.in(bit_extender_1_out), .\dist (5'b00010), .out(shifter_1_out));
  Adder #(.width(32)) adder_2 (.a(adder_1_out), .b(shifter_1_out), .out(adder_2_out));  // open: cin, cout
  Multiplexer #(.select(2), .width(32)) multiplexer_1 (
    .in0(adder_1_out), .in1({adder_1_out[31:28], addr, 2'b00}), .in2(adder_2_out), .out(npc), .sel(npcctrol));  // open: in3, en
endmodule
