// Logisim project cpuY.circ as structural Verilog: 16 circuits, main circuit main
module main (
  input  clk,
  input  clr
);

  wire and_1_out, and_2_out, and_3_out, comparator_1_eq, comparator_2_eq, comparator_3_eq, ctrl_1_alusrc,
       ctrl_1_extop, ctrl_1_jump, ctrl_1_memwrite, ctrl_1_mentoreg, ctrl_1_npcctrol, ctrl_1_regdst,
       ctrl_1_regwrite, exe_mem_1_memtoregm, exe_mem_1_memwritem, exe_mem_1_regwritem, id_exe_1_alusrce,
       id_exe_1_memtorege, id_exe_1_memwritee, id_exe_1_regdste, id_exe_1_regwritee, mem_wb_1_memtoregw,
       mem_wb_1_regwritew, or_1_out, pause_1_id_exe_we, pause_1_if_id_we, pause_1_pc_we;
  wire [1:0] beq_reandpa_1_id_mux1_plus, beq_reandpa_1_id_mux2_plus, redirect_1_exe_mux1_plus,
       redirect_1_exe_mux2_plus;
  wire [2:0] ctrl_1_aluctr, id_exe_1_aluctre;
  wire [3:0] rf_1_r8, rf_1_r8_2, rf_1_r8_3, rf_1_r8_4, rf_1_r8_5, rf_1_r8_6, rf_1_r8_7, rf_1_r8_8,
       rf_1_r17_2, rf_1_r17_3, rf_1_r17_4, rf_1_r18, rf_1_r18_2, rf_1_r18_3, rf_1_r18_4, rf_1_r18_5,
       rf_1_r18_6, rf_1_r18_7, rf_1_r18_8;
  wire [4:0] exe_mem_1_writeregm, id_exe_1_rde, id_exe_1_rse, id_exe_1_rte, if_id_1_rd_2, if_id_1_rs,
       if_id_1_rt, mem_wb_1_writeregw, multiplexer_7_out;
  wire [5:0] if_id_1_func, if_id_1_op;
  wire [15:0] if_id_1_imm;
  wire [25:0] if_id_1_target;
  wire [31:0] adder_1_out, adder_2_out, alu_1_out_4, dm_1_output, ep_1_eximm, exe_mem_1_aluoutm,
       exe_mem_1_rd2m, id_exe_1_imme, id_exe_1_rd1e, id_exe_1_rd2e, if_id_1_pcnd, im_1_rd, mem_wb_1_aluoutw,
       mem_wb_1_outputw, multiplexer_1_out, multiplexer_2_out, multiplexer_3_out, multiplexer_4_out,
       multiplexer_5_out, multiplexer_6_out, multiplexer_8_out, multiplexer_9_out, multiplexer_10_out,
       pc_1_data, rf_1_qa, rf_1_qb, rf_1_r16, rf_1_r17, shifter_1_out, target_1_jmp_adr;

  Multiplexer #(.width(32), .enable("false")) multiplexer_1 (
    .in0(adder_1_out), .in1(adder_2_out), .out(multiplexer_1_out), .sel(and_3_out));
  Multiplexer #(.width(32), .enable("false")) multiplexer_2 (
    .in0(multiplexer_1_out), .in1(target_1_jmp_adr), .out(multiplexer_2_out), .sel(ctrl_1_jump));
  PC pc_1 (.adr(multiplexer_2_out), .we(pause_1_pc_we), .clk(clk), .clr(clr), .data(pc_1_data));
  Hex_Digit_Display hex_digit_display_1 (.value(rf_1_r8_8));  // open: dp
  Hex_Digit_Display hex_digit_display_2 (.value(rf_1_r8_7));  // open: dp
  IM im_1 (.addr(pc_1_data), .rd(im_1_rd));
  Adder #(.width(32)) adder_1 (.a(pc_1_data), .b(32'h4), .out(adder_1_out));  // open: cin, cout
  or or_1 (or_1_out, ctrl_1_jump, and_3_out);
  Hex_Digit_Display hex_digit_display_3 (.value(rf_1_r8_6));  // open: dp
  Hex_Digit_Display hex_digit_display_4 (.value(rf_1_r8_5));  // open: dp
  IF_ID if_id_1 (
    .clk(clk), .we(pause_1_if_id_we), .rd(im_1_rd), .pcn(adder_1_out), .clr(clr), .jmp(or_1_out),
    .op(if_id_1_op), .func(if_id_1_func), .rs(if_id_1_rs), .rt(if_id_1_rt), .rd_2(if_id_1_rd_2),
    .imm(if_id_1_imm), .target(if_id_1_target), .pcnD(if_id_1_pcnd));
  Hex_Digit_Display hex_digit_display_5 (.value(rf_1_r8_4));  // open: dp
  Hex_Digit_Display hex_digit_display_6 (.value(rf_1_r8_3));  // open: dp
  Hex_Digit_Display hex_digit_display_7 (.value(im_1_rd[31:28]));  // open: dp
  Hex_Digit_Display hex_digit_display_8 (.value(im_1_rd[27:24]));  // open: dp
  Comparator #(.width(5)) comparator_1 (.a(if_id_1_rs), .b(mem_wb_1_writeregw), .eq(comparator_1_eq));  // open: gt, lt
  Comparator #(.width(5)) comparator_2 (.a(if_id_1_rt), .b(mem_wb_1_writeregw), .eq(comparator_2_eq));  // open: gt, lt
  Hex_Digit_Display hex_digit_display_9 (.value(rf_1_r8));  // open: dp
  Hex_Digit_Display hex_digit_display_10 (.value(rf_1_r8_2));  // open: dp
  Hex_Digit_Display hex_digit_display_11 (.value(im_1_rd[23:20]));  // open: dp
  Hex_Digit_Display hex_digit_display_12 (.value(im_1_rd[19:16]));  // open: dp
  and and_1 (and_1_out, comparator_1_eq, mem_wb_1_regwritew);
  and and_2 (and_2_out, comparator_2_eq, mem_wb_1_regwritew);
  CTRL ctrl_1 (
    .ALUctr(ctrl_1_aluctr), .RegWrite(ctrl_1_regwrite), .MenToReg(ctrl_1_mentoreg),
    .MemWrite(ctrl_1_memwrite), .npcctrol(ctrl_1_npcctrol), .ALUsrc(ctrl_1_alusrc), .RegDst(ctrl_1_regdst),
    .ExtOp(ctrl_1_extop), .jump(ctrl_1_jump), .op(if_id_1_op), .func(if_id_1_func));
  RF rf_1 (
    .clr(clr), .rw(mem_wb_1_writeregw), .clk(clk), .data(multiplexer_10_out), .we(mem_wb_1_regwritew),
    .r8({rf_1_r8_8, rf_1_r8_7, rf_1_r8_6, rf_1_r8_5, rf_1_r8_4, rf_1_r8_3, rf_1_r8_2, rf_1_r8}),
    .r16(rf_1_r16),
    .r17({rf_1_r17[31:24], rf_1_r17_4, rf_1_r17_3, rf_1_r17[15:12], rf_1_r17_2, rf_1_r17[7:0]}),
    .r18({rf_1_r18_8, rf_1_r18_7, rf_1_r18_6, rf_1_r18_5, rf_1_r18_4, rf_1_r18_3, rf_1_r18_2, rf_1_r18}),
    .qb(rf_1_qb), .rb(if_id_1_rt), .qa(rf_1_qa), .ra(if_id_1_rs));
  EP ep_1 (.imm(if_id_1_imm), .ExtOp(ctrl_1_extop), .eximm(ep_1_eximm));
  target target_1 (.addr_25_0(if_id_1_target), .PCplus4(if_id_1_pcnd), .jmp_adr(target_1_jmp_adr));
  Hex_Digit_Display hex_digit_display_13 (.value(im_1_rd[11:8]));  // open: dp
  Hex_Digit_Display hex_digit_display_14 (.value(im_1_rd[15:12]));  // open: dp
  Hex_Digit_Display hex_digit_display_15 (.value(rf_1_r16[27:24]));  // open: dp
  Hex_Digit_Display hex_digit_display_16 (.value(rf_1_r16[31:28]));  // open: dp
  Hex_Digit_Display hex_digit_display_17 (.value(im_1_rd[3:0]));  // open: dp
  Hex_Digit_Display hex_digit_display_18 (.value(im_1_rd[7:4]));  // open: dp
  Multiplexer #(.width(32), .enable("false")) multiplexer_3 (
    .in0(rf_1_qa), .in1(multiplexer_10_out), .out(multiplexer_3_out), .sel(and_1_out));
  Multiplexer #(.width(32), .enable("false")) multiplexer_4 (
    .in0(rf_1_qb), .in1(multiplexer_10_out), .out(multiplexer_4_out), .sel(and_2_out));
  Shifter #(.width(32)) shifter_1 (.in(ep_1_eximm), .\dist (5'b00010), .out(shifter_1_out));
  Hex_Digit_Display hex_digit_display_19 (.value(rf_1_r16[19:16]));  // open: dp
  Hex_Digit_Display hex_digit_display_20 (.value(rf_1_r16[23:20]));  // open: dp
  Multiplexer #(.select(2), .width(32), .enable("false")) multiplexer_5 (
    .in0(multiplexer_3_out), .in1(alu_1_out_4), .in2(exe_mem_1_aluoutm), .in3(dm_1_output),
    .out(multiplexer_5_out), .sel(beq_reandpa_1_id_mux2_plus));
  Comparator #(.width(32)) comparator_3 (
    .a(multiplexer_5_out), .b(multiplexer_6_out), .eq(comparator_3_eq));  // open: gt, lt
  Multiplexer #(.select(2), .width(32), .enable("false")) multiplexer_6 (
    .in0(multiplexer_4_out), .in1(alu_1_out_4), .in2(exe_mem_1_aluoutm), .in3(dm_1_output),
    .out(multiplexer_6_out), .sel(beq_reandpa_1_id_mux1_plus));
  Adder #(.width(32)) adder_2 (.a(shifter_1_out), .b(if_id_1_pcnd), .out(adder_2_out));  // open: cin, cout
  pause pause_1 (
    .IF_ID_rs(if_id_1_rs), .IF_ID_rt(if_id_1_rt), .ID_EXE_rt(id_exe_1_rte),
    .ID_EXE_MemToReg(id_exe_1_memtorege), .PC_we(pause_1_pc_we), .IF_ID_we(pause_1_if_id_we),
    .ID_EXE_we(pause_1_id_exe_we));
  Hex_Digit_Display hex_digit_display_21 (.value(rf_1_r16[11:8]));  // open: dp
  Hex_Digit_Display hex_digit_display_22 (.value(rf_1_r16[15:12]));  // open: dp
  and and_3 (and_3_out, ctrl_1_npcctrol, comparator_3_eq);
  Hex_Digit_Display hex_digit_display_23 (.value(rf_1_r16[3:0]));  // open: dp
  Hex_Digit_Display hex_digit_display_24 (.value(rf_1_r16[7:4]));  // open: dp
  ID_EXE id_exe_1 (
    .clk(clk), .RegWriteD(ctrl_1_regwrite), .MemToRegD(ctrl_1_mentoreg), .MemWriteD(ctrl_1_memwrite),
    .ALUctrD(ctrl_1_aluctr), .ALUsrcD(ctrl_1_alusrc), .RegDstD(ctrl_1_regdst), .RD1D(multiplexer_5_out),
    .RD2D(multiplexer_6_out), .rtD(if_id_1_rt), .rdD(if_id_1_rd_2), .immD(ep_1_eximm), .rsD(if_id_1_rs),
    .we(pause_1_id_exe_we), .RegWriteE(id_exe_1_regwritee), .MemToRegE(id_exe_1_memtorege),
    .MemWriteE(id_exe_1_memwritee), .ALUctrE(id_exe_1_aluctre), .ALUsrcE(id_exe_1_alusrce),
    .RegDstE(id_exe_1_regdste), .RD1E(id_exe_1_rd1e), .RD2E(id_exe_1_rd2e), .rtE(id_exe_1_rte),
    .rdE(id_exe_1_rde), .immE(id_exe_1_imme), .rsE(id_exe_1_rse));
  Hex_Digit_Display hex_digit_display_25 (.value(rf_1_r17[31:28]));  // open: dp
  Multiplexer #(.width(5), .enable("false")) multiplexer_7 (
    .in0(id_exe_1_rte), .in1(id_exe_1_rde), .out(multiplexer_7_out), .sel(id_exe_1_regdste));
  Hex_Digit_Display hex_digit_display_26 (.value(rf_1_r17[27:24]));  // open: dp
  Hex_Digit_Display hex_digit_display_27 (.value(rf_1_r17_4));  // open: dp
  Multiplexer #(.select(2), .width(32), .enable("false")) multiplexer_8 (
    .in0(id_exe_1_rd1e), .in1(exe_mem_1_aluoutm), .in2(multiplexer_10_out), .out(multiplexer_8_out),
    .sel(redirect_1_exe_mux2_plus));  // open: in3
  redirect redirect_1 (
    .ID_EXE_ALUsrc(id_exe_1_alusrce), .ID_EXE_RS(id_exe_1_rse), .ID_EXE_RT(id_exe_1_rte),
    .EXE_MEM_WriteReg(exe_mem_1_writeregm), .EXE_MEM_RegWrite(exe_mem_1_regwritem),
    .MEM_WB_WriteReg(mem_wb_1_writeregw), .MEM_WB_RegWrite(mem_wb_1_regwritew),
    .EXE_MUX1_plus(redirect_1_exe_mux1_plus), .EXE_MUX2_plus(redirect_1_exe_mux2_plus));
  Hex_Digit_Display hex_digit_display_28 (.value(rf_1_r17_3));  // open: dp
  Hex_Digit_Display hex_digit_display_29 (.value(rf_1_r17[15:12]));  // open: dp
  beq_reANDpa beq_reandpa_1 (
    .IF_ID_rs(if_id_1_rs), .IF_ID_rt(if_id_1_rt), .EXE_MUXout_minus(multiplexer_7_out),
    .ID_EXE_RegWrite(id_exe_1_regwritee), .EXE_MEM_MemWrite(exe_mem_1_memwritem),
    .EXE_MEM_WriteReg(exe_mem_1_writeregm), .EXE_MEM_RegWrite(exe_mem_1_regwritem),
    .ID_MUX1_plus(beq_reandpa_1_id_mux1_plus), .ID_MUX2_plus(beq_reandpa_1_id_mux2_plus));
  Hex_Digit_Display hex_digit_display_30 (.value(rf_1_r17[7:4]));  // open: dp
  Hex_Digit_Display hex_digit_display_31 (.value(rf_1_r17_2));  // open: dp
  Multiplexer #(.select(2), .width(32), .enable("false")) multiplexer_9 (
    .in0(id_exe_1_rd2e), .in1(exe_mem_1_aluoutm), .in2(multiplexer_10_out), .in3(id_exe_1_imme),
    .out(multiplexer_9_out), .sel(redirect_1_exe_mux1_plus));
  Hex_Digit_Display hex_digit_display_32 (.value(rf_1_r17[3:0]));  // open: dp
  ALU alu_1 (.aluc(id_exe_1_aluctre), .in_2(multiplexer_8_out), .B(multiplexer_9_out), .out_4(alu_1_out_4));
  Hex_Digit_Display hex_digit_display_33 (.value(rf_1_r18_8));  // open: dp
  EXE_MEM exe_mem_1 (
    .clk(clk), .RegWriteE(id_exe_1_regwritee), .MemToRegE(id_exe_1_memtorege),
    .MemWriteE(id_exe_1_memwritee), .aluoutE(alu_1_out_4), .RD2E(id_exe_1_rd2e),
    .WriteRegE(multiplexer_7_out), .clr(clr), .RegWriteM(exe_mem_1_regwritem),
    .MemToRegM(exe_mem_1_memtoregm), .MemWriteM(exe_mem_1_memwritem), .aluoutM(exe_mem_1_aluoutm),
    .RD2M(exe_mem_1_rd2m), .WriteRegM(exe_mem_1_writeregm));
  Hex_Digit_Display hex_digit_display_34 (.value(rf_1_r18_7));  // open: dp
  Hex_Digit_Display hex_digit_display_35 (.value(rf_1_r18_6));  // open: dp
  DM dm_1 (
    .address(exe_mem_1_aluoutm), .\input (exe_mem_1_rd2m), .we(exe_mem_1_memwritem), .clk(clk),
    .\output (dm_1_output));  // open: clr
  Hex_Digit_Display hex_digit_display_36 (.value(rf_1_r18_5));  // open: dp
  Hex_Digit_Display hex_digit_display_37 (.value(rf_1_r18_4));  // open: dp
  Hex_Digit_Display hex_digit_display_38 (.value(rf_1_r18_2));  // open: dp
  Hex_Digit_Display hex_digit_display_39 (.value(rf_1_r18_3));  // open: dp
  MEM_WB mem_wb_1 (
    .clk(clk), .RegWriteM(exe_mem_1_regwritem), .MemToRegM(exe_mem_1_memtoregm), .aluoutM(exe_mem_1_aluoutm),
    .outputM(dm_1_output), .WriteRegM(exe_mem_1_writeregm), .clr(clr), .RegWriteW(mem_wb_1_regwritew),
    .MemToRegW(mem_wb_1_memtoregw), .aluoutW(mem_wb_1_aluoutw), .outputW(mem_wb_1_outputw),
    .WriteRegW(mem_wb_1_writeregw));
  Hex_Digit_Display hex_digit_display_40 (.value(rf_1_r18));  // open: dp
  Multiplexer #(.width(32), .enable("false")) multiplexer_10 (
    .in0(mem_wb_1_aluoutw), .in1(mem_wb_1_outputw), .out(multiplexer_10_out), .sel(mem_wb_1_memtoregw));

  // Notes on the sheet:
  //   r8
  //   IR
  //   IF/ID
  //   r16
  //   1
  //   2
  //   ID/EXE
  //   r17
  //   2
  //   1
  //   r18
  //   EXE/MEM
  //   MEM/WB
endmodule

module PC (
  input  [31:0] adr,
  input  we,
  input  clk,
  input  clr,
  output [31:0] data
);

  Register #(.width(32)) register_1 (.D(adr), .en(we), .Q(data), .clk(clk), .clr(clr));
endmodule

module IM (
  input  [31:0] addr,
  output [31:0] rd
);

  ROM #(.addrWidth(24), .dataWidth(32)) rom_1 (.addr(addr[23:0]), .data(rd));  // open: sel

  // Notes on the sheet:
  //   contents of rom_1 (hex, n*v repeats v):
  //   20100000 0 0 0 20110000 0 0 0 9024 0 0 0 2008000a 0 0 0 12280004 0 0 0 2129020 0 0 0 22100001 0 0 0
  //   22310001 0 0 0 8000004 0 0 0 ac120040 0 0 0 8c100040
endmodule

module CTRL (
  input  [5:0] op,
  input  [5:0] func,
  output RegWrite,
  output MenToReg,
  output MemWrite,
  output npcctrol,
  output [2:0] ALUctr,
  output ALUsrc,
  output RegDst,
  output ExtOp,
  output jump
);

  wire addi_out, and_1_out, and_2_out, and_3_out, and_4_out;
  wire [1:1] ori_out;
  wire [2:0] or_4_out;

  and R_type (RegDst, ~op[5], ~op[4], ~op[3], ~op[2], ~op[1], ~op[0]);  // AND_Gate
  and ori (ori_out[1], ~op[5], ~op[4], op[3], op[2], ~op[1], op[0]);  // AND_Gate
  and lw (MenToReg, op[5], ~op[4], ~op[3], ~op[2], op[1], op[0]);  // AND_Gate
  and sw (MemWrite, op[5], ~op[4], op[3], ~op[2], op[1], op[0]);  // AND_Gate
  and beg (npcctrol, ~op[5], ~op[4], ~op[3], op[2], ~op[1], ~op[0]);  // AND_Gate
  and u_jump (jump, ~op[5], ~op[4], ~op[3], ~op[2], op[1], ~op[0]);  // AND_Gate
  and addi (addi_out, ~op[5], ~op[4], op[3], ~op[2], ~op[1], ~op[0]);  // AND_Gate
  or or_1 (RegWrite, RegDst, addi_out, ori_out[1], MenToReg);
  or or_2 (ALUsrc, addi_out, ori_out[1], MenToReg, MemWrite);
  or or_3 (ExtOp, MenToReg, npcctrol, MemWrite);
  and and_1 (and_1_out, ~func[3], func[2], ~func[1], ~func[0]);  // AND_Gate
  and and_2 (and_2_out, func[3], ~func[2], func[1], ~func[0]);  // AND_Gate
  Multiplexer #(.width(3)) multiplexer_1 (
    .in0({npcctrol, ori_out[1], RegDst}), .in1(or_4_out), .out(ALUctr), .sel(RegDst));  // open: en
  and and_3 (and_3_out, ~func[3], func[2], ~func[1], func[0]);  // AND_Gate
  and and_4 (and_4_out, func[3], ~func[2], func[1], ~func[0]);  // AND_Gate
  and and_5 (or_4_out[2], ~func[2], func[1], ~func[0]);  // AND_Gate
  or or_4 (or_4_out[0], and_1_out, and_2_out);
  or or_5 (or_4_out[1], and_3_out, and_4_out);
endmodule

module RF (
  input  clr,
  input  [4:0] rw,
  input  [4:0] rb,
  input  clk,
  input  [31:0] data,
  input  [4:0] ra,
  input  we,
  output [31:0] qb,
  output [31:0] qa,
  output [31:0] r8,
  output [31:0] r16,
  output [31:0] r17,
  output [31:0] r18
);

  wire and_1_out, and_2_out, and_3_out, and_4_out, and_5_out, and_6_out, and_7_out, and_8_out, and_9_out,
       and_10_out, and_11_out, and_12_out, and_13_out, and_14_out, and_15_out, and_16_out, and_17_out,
       and_18_out, and_19_out, and_20_out, and_21_out, and_22_out, and_23_out, and_24_out, and_25_out,
       and_26_out, and_27_out, and_28_out, and_29_out, and_30_out, and_31_out, and_32_out, decoder_1_out0,
       decoder_1_out1, decoder_1_out2, decoder_1_out3, decoder_1_out4, decoder_1_out5, decoder_1_out6,
       decoder_1_out7, decoder_1_out8, decoder_1_out9, decoder_1_out10, decoder_1_out11, decoder_1_out12,
       decoder_1_out13, decoder_1_out14, decoder_1_out15, decoder_1_out16, decoder_1_out17, decoder_1_out18,
       decoder_1_out19, decoder_1_out20, decoder_1_out21, decoder_1_out22, decoder_1_out23, decoder_1_out24,
       decoder_1_out25, decoder_1_out26, decoder_1_out27, decoder_1_out28, decoder_1_out29, decoder_1_out30,
       decoder_1_out31;
  wire [31:0] r0_q, r1_q, r2_q, r3_q, r4_q, r5_q, r6_q, r7_q, r9_q, r10_q, r11_q, r12_q, r13_q, r14_q, r15_q,
       r19_q, r20_q, r21_q, r22_q, r23_q, r24_q, r25_q, r26_q, r27_q, r28_q, r29_q, r30_q, r31_q;

  Decoder #(.select(5), .enable("false")) decoder_1 (
    .out0(decoder_1_out0), .out1(decoder_1_out1), .out2(decoder_1_out2), .out3(decoder_1_out3),
    .out4(decoder_1_out4), .out5(decoder_1_out5), .out6(decoder_1_out6), .out7(decoder_1_out7),
    .out8(decoder_1_out8), .out9(decoder_1_out9), .out10(decoder_1_out10), .out11(decoder_1_out11),
    .out12(decoder_1_out12), .out13(decoder_1_out13), .out14(decoder_1_out14), .out15(decoder_1_out15),
    .out16(decoder_1_out16), .out17(decoder_1_out17), .out18(decoder_1_out18), .out19(decoder_1_out19),
    .out20(decoder_1_out20), .out21(decoder_1_out21), .out22(decoder_1_out22), .out23(decoder_1_out23),
    .out24(decoder_1_out24), .out25(decoder_1_out25), .out26(decoder_1_out26), .out27(decoder_1_out27),
    .out28(decoder_1_out28), .out29(decoder_1_out29), .out30(decoder_1_out30), .out31(decoder_1_out31),
    .sel(rw));
  and and_1 (and_1_out, decoder_1_out16, we);
  and and_2 (and_2_out, decoder_1_out17, we);
  and and_3 (and_3_out, decoder_1_out18, we);
  and and_4 (and_4_out, decoder_1_out19, we);
  and and_5 (and_5_out, decoder_1_out20, we);
  and and_6 (and_6_out, decoder_1_out21, we);
  and and_7 (and_7_out, decoder_1_out22, we);
  and and_8 (and_8_out, decoder_1_out23, we);
  and and_9 (and_9_out, decoder_1_out24, we);
  and and_10 (and_10_out, decoder_1_out25, we);
  and and_11 (and_11_out, decoder_1_out26, we);
  and and_12 (and_12_out, decoder_1_out27, we);
  and and_13 (and_13_out, decoder_1_out28, we);
  and and_14 (and_14_out, decoder_1_out29, we);
  and and_15 (and_15_out, decoder_1_out30, we);
  and and_16 (and_16_out, decoder_1_out31, we);
  and and_17 (and_17_out, decoder_1_out0, we);
  and and_18 (and_18_out, decoder_1_out1, we);
  buf and_19 (and_19_out, decoder_1_out2);  // AND_Gate
  and and_20 (and_20_out, decoder_1_out3, we);
  and and_21 (and_21_out, decoder_1_out4, we);
  and and_22 (and_22_out, decoder_1_out5, we);
  and and_23 (and_23_out, decoder_1_out6, we);
  and and_24 (and_24_out, decoder_1_out7, we);
  and and_25 (and_25_out, decoder_1_out8, we);
  and and_26 (and_26_out, decoder_1_out9, we);
  and and_27 (and_27_out, decoder_1_out10, we);
  and and_28 (and_28_out, decoder_1_out11, we);
  and and_29 (and_29_out, decoder_1_out12, we);
  and and_30 (and_30_out, decoder_1_out13, we);
  and and_31 (and_31_out, decoder_1_out14, we);
  and and_32 (and_32_out, decoder_1_out15, we);
  Register #(.width(32)) r0 (.D(data), .en(and_17_out), .Q(r0_q), .clk(clk), .clr(clr));
  Register #(.width(32)) r4 (.D(data), .en(and_21_out), .Q(r4_q), .clk(clk), .clr(clr));
  Register #(.width(32)) u_r8 (.D(data), .en(and_25_out), .Q(r8), .clk(clk), .clr(clr));
  Register #(.width(32)) r12 (.D(data), .en(and_29_out), .Q(r12_q), .clk(clk), .clr(clr));
  Register #(.width(32)) u_r16 (.D(data), .en(and_1_out), .Q(r16), .clk(clk), .clr(clr));
  Register #(.width(32)) r20 (.D(data), .en(and_5_out), .Q(r20_q), .clk(clk), .clr(clr));
  Register #(.width(32)) r24 (.en(and_9_out), .Q(r24_q), .clk(clk), .clr(clr));  // open: D
  Register #(.width(32)) r28 (.D(data), .en(and_13_out), .Q(r28_q), .clk(clk), .clr(clr));
  Register #(.width(32)) r1 (.D(data), .en(and_18_out), .Q(r1_q), .clk(clk), .clr(clr));
  Register #(.width(32)) r5 (.D(data), .en(and_22_out), .Q(r5_q), .clk(clk), .clr(clr));
  Register #(.width(32)) r9 (.D(data), .en(and_26_out), .Q(r9_q), .clk(clk), .clr(clr));
  Register #(.width(32)) r13 (.D(data), .en(and_30_out), .Q(r13_q), .clk(clk), .clr(clr));
  Register #(.width(32)) register_1 (.D(data), .en(and_2_out), .Q(r17), .clk(clk), .clr(clr));
  Register #(.width(32)) r21 (.D(data), .en(and_6_out), .Q(r21_q), .clk(clk), .clr(clr));
  Register #(.width(32)) r25 (.en(and_10_out), .Q(r25_q), .clk(clk), .clr(clr));  // open: D
  Register #(.width(32)) r29 (.D(data), .en(and_14_out), .Q(r29_q), .clk(clk), .clr(clr));
  Register #(.width(32)) r2 (.D(data), .en(and_19_out), .Q(r2_q), .clk(clk), .clr(clr));
  Register #(.width(32)) r6 (.D(data), .en(and_23_out), .Q(r6_q), .clk(clk), .clr(clr));
  Register #(.width(32)) r10 (.D(data), .en(and_27_out), .Q(r10_q), .clk(clk), .clr(clr));
  Register #(.width(32)) r14 (.D(data), .en(and_31_out), .Q(r14_q), .clk(clk), .clr(clr));
  Register #(.width(32)) u_r18 (.D(data), .en(and_3_out), .Q(r18), .clk(clk), .clr(clr));
  Register #(.width(32)) r22 (.D(data), .en(and_7_out), .Q(r22_q), .clk(clk), .clr(clr));
  Register #(.width(32)) r26 (.en(and_11_out), .Q(r26_q), .clk(clk), .clr(clr));  // open: D
  Register #(.width(32)) r30 (.D(data), .en(and_15_out), .Q(r30_q), .clk(clk), .clr(clr));
  Register #(.width(32)) r3 (.D(data), .en(and_20_out), .Q(r3_q), .clk(clk), .clr(clr));
  Register #(.width(32)) r7 (.D(data), .en(and_24_out), .Q(r7_q), .clk(clk), .clr(clr));
  Register #(.width(32)) r11 (.D(data), .en(and_28_out), .Q(r11_q), .clk(clk), .clr(clr));
  Register #(.width(32)) r15 (.D(data), .en(and_32_out), .Q(r15_q), .clk(clk), .clr(clr));
  Register #(.width(32)) r19 (.D(data), .en(and_4_out), .Q(r19_q), .clk(clk), .clr(clr));
  Register #(.width(32)) r23 (.D(data), .en(and_8_out), .Q(r23_q), .clk(clk), .clr(clr));
  Register #(.width(32)) r27 (.en(and_12_out), .Q(r27_q), .clk(clk), .clr(clr));  // open: D
  Register #(.width(32)) r31 (.D(data), .en(and_16_out), .Q(r31_q), .clk(clk), .clr(clr));
  Multiplexer #(.select(5), .width(32)) multiplexer_1 (
    .in0(r0_q), .in1(r1_q), .in2(r2_q), .in3(r3_q), .in4(r4_q), .in5(r5_q), .in6(r6_q), .in7(r7_q), .in8(r8),
    .in9(r9_q), .in10(r10_q), .in11(r11_q), .in12(r12_q), .in13(r13_q), .in14(r14_q), .in15(r15_q),
    .in16(r16), .in17(r17), .in18(r18), .in19(r19_q), .in20(r20_q), .in21(r21_q), .in22(r22_q), .in23(r23_q),
    .in24(r24_q), .in25(r25_q), .in26(r26_q), .in27(r27_q), .in28(r28_q), .in29(r29_q), .in30(r30_q),
    .in31(r31_q), .out(qb), .sel(rb));  // open: en
  Multiplexer #(.select(5), .width(32)) multiplexer_2 (
    .in0(r0_q), .in1(r1_q), .in2(r2_q), .in3(r3_q), .in4(r4_q), .in5(r5_q), .in6(r6_q), .in7(r7_q), .in8(r8),
    .in9(r9_q), .in10(r10_q), .in11(r11_q), .in12(r12_q), .in13(r13_q), .in14(r14_q), .in15(r15_q),
    .in16(r16), .in17(r17), .in18(r18), .in19(r19_q), .in20(r20_q), .in21(r21_q), .in22(r22_q), .in23(r23_q),
    .in24(r24_q), .in25(r25_q), .in26(r26_q), .in27(r27_q), .in28(r28_q), .in29(r29_q), .in30(r30_q),
    .in31(r31_q), .out(qa), .sel(ra));  // open: en

  // Notes on the sheet:
  //   mux_b
  //   mux_a
endmodule

module EP (
  input  [15:0] imm,
  input  ExtOp,
  output [31:0] eximm
);

  wire [31:0] bit_extender_1_out, bit_extender_2_out;

  assign bit_extender_1_out = {{16{1'b0}}, imm};  // Bit_Extender bit_extender_1
  assign bit_extender_2_out = {{16{imm[15]}}, imm};  // Bit_Extender bit_extender_2
  Multiplexer #(.width(32)) multiplexer_1 (
    .in0(bit_extender_1_out), .in1(bit_extender_2_out), .out(eximm), .sel(ExtOp));  // open: en
endmodule

module target (
  input  [25:0] addr_25_0,
  input  [31:0] PCplus4,
  output [31:0] jmp_adr
);


  assign jmp_adr = {PCplus4[31:28], addr_25_0, 2'b00};
endmodule

module ALU (
  input  [2:0] aluc,
  input  [31:0] in_2,
  input  [31:0] B,
  output [31:0] out_4
);

  wire [31:0] adder_1_out, and_1_out, or_1_out, subtractor_1_out;

  Adder #(.width(32)) adder_1 (.a(in_2), .b(B), .out(adder_1_out));  // open: cin, cout
  Subtractor #(.width(32)) subtractor_1 (.a(in_2), .b(B), .out(subtractor_1_out));  // open: bin, bout
  assign or_1_out = in_2 | B;  // OR_Gate or_1, 32 bits wide
  assign and_1_out = in_2 & B;  // AND_Gate and_1, 32 bits wide
  Multiplexer #(.select(3), .width(32), .enable("false")) multiplexer_1 (
    .in0(adder_1_out), .in1(and_1_out), .in2(or_1_out), .in4(subtractor_1_out), .out(out_4), .sel(aluc));  // open: in3, in5, in6, in7

  // Notes on the sheet:
  //   A
  //   alu_out
endmodule

module DM (
  input  [31:0] address,
  input  [31:0] \input ,
  input  we,
  input  clk,
  input  clr,
  output [31:0] \output 
);

  RAM #(.addrWidth(24), .dataWidth(32), .bus("separate")) ram_1 (
    .addr(address[23:0]), .din(\input ), .data(\output ), .str(we), .clk(clk), .clr(clr));  // open: sel, ld
endmodule

module IF_ID (
  input  clk,
  input  we,
  input  [31:0] rd,
  input  [31:0] pcn,
  input  clr,
  input  jmp,
  output [5:0] op,
  output [5:0] func,
  output [4:0] rs,
  output [4:0] rt,
  output [4:0] rd_2,
  output [15:0] imm,
  output [25:0] target,
  output [31:0] pcnD
);

  wire multiplexer_1_out, register_1_q;

  Register #(.width(1)) register_1 (.D(jmp), .en(we), .Q(register_1_q), .clk(clk), .clr(register_1_q));
  Multiplexer multiplexer_1 (.in0(clr), .in1(register_1_q), .out(multiplexer_1_out), .sel(jmp));  // open: en
  Register #(.width(32)) register_2 (
    .D(rd), .en(we), .Q({op, rs, rt, imm[15:6], func}), .clk(clk), .clr(multiplexer_1_out));
  Register #(.width(32)) register_3 (.D(pcn), .en(we), .Q(pcnD), .clk(clk), .clr(multiplexer_1_out));

  assign imm[5:0] = func;
  assign rd_2 = imm[15:11];
  assign target = {rs, rt, imm[15:6], func};
endmodule

module ID_EXE (
  input  clk,
  input  RegWriteD,
  input  MemToRegD,
  input  MemWriteD,
  input  [2:0] ALUctrD,
  input  ALUsrcD,
  input  RegDstD,
  input  [31:0] RD1D,
  input  [31:0] RD2D,
  input  [4:0] rtD,
  input  [4:0] rdD,
  input  [31:0] immD,
  input  [4:0] rsD,
  input  we,
  output RegWriteE,
  output MemToRegE,
  output MemWriteE,
  output [2:0] ALUctrE,
  output ALUsrcE,
  output RegDstE,
  output [31:0] RD1E,
  output [31:0] RD2E,
  output [4:0] rtE,
  output [4:0] rdE,
  output [31:0] immE,
  output [4:0] rsE
);

  wire not_1_out, register_13_q;

  not not_1 (not_1_out, we);
  Register #(.width(1)) register_1 (.D(RegWriteD), .en(1'b1), .Q(RegWriteE), .clk(clk), .clr(register_13_q));
  Register #(.width(1)) register_2 (.D(MemToRegD), .en(1'b1), .Q(MemToRegE), .clk(clk), .clr(register_13_q));
  Register #(.width(1)) register_3 (.D(MemWriteD), .en(1'b1), .Q(MemWriteE), .clk(clk), .clr(register_13_q));
  Register #(.width(3)) register_4 (.D(ALUctrD), .en(1'b1), .Q(ALUctrE), .clk(clk), .clr(register_13_q));
  Register #(.width(1)) register_5 (.D(ALUsrcD), .en(1'b1), .Q(ALUsrcE), .clk(clk), .clr(register_13_q));
  Register #(.width(1)) register_6 (.D(RegDstD), .en(1'b1), .Q(RegDstE), .clk(clk), .clr(register_13_q));
  Register #(.width(32)) register_7 (.D(RD1D), .en(1'b1), .Q(RD1E), .clk(clk), .clr(register_13_q));
  Register #(.width(32)) register_8 (.D(RD2D), .en(1'b1), .Q(RD2E), .clk(clk), .clr(register_13_q));
  Register #(.width(5)) register_9 (.D(rtD), .en(1'b1), .Q(rtE), .clk(clk), .clr(register_13_q));
  Register #(.width(5)) register_10 (.D(rdD), .en(1'b1), .Q(rdE), .clk(clk), .clr(register_13_q));
  Register #(.width(32)) register_11 (.D(immD), .en(1'b1), .Q(immE), .clk(clk), .clr(register_13_q));
  Register #(.width(5)) register_12 (.D(rsD), .en(1'b1), .Q(rsE), .clk(clk), .clr(register_13_q));
  Register #(.width(1)) register_13 (.D(not_1_out), .en(1'b1), .Q(register_13_q), .clk(clk), .clr(register_13_q));
endmodule

module EXE_MEM (
  input  clk,
  input  RegWriteE,
  input  MemToRegE,
  input  MemWriteE,
  input  [31:0] aluoutE,
  input  [31:0] RD2E,
  input  [4:0] WriteRegE,
  input  clr,
  output RegWriteM,
  output MemToRegM,
  output MemWriteM,
  output [31:0] aluoutM,
  output [31:0] RD2M,
  output [4:0] WriteRegM
);

  Register #(.width(1)) register_1 (.D(RegWriteE), .en(1'b1), .Q(RegWriteM), .clk(clk), .clr(clr));
  Register #(.width(1)) register_2 (.D(MemToRegE), .en(1'b1), .Q(MemToRegM), .clk(clk), .clr(clr));
  Register #(.width(1)) register_3 (.D(MemWriteE), .en(1'b1), .Q(MemWriteM), .clk(clk), .clr(clr));
  Register #(.width(32)) register_4 (.D(aluoutE), .en(1'b1), .Q(aluoutM), .clk(clk), .clr(clr));
  Register #(.width(32)) register_5 (.D(RD2E), .en(1'b1), .Q(RD2M), .clk(clk), .clr(clr));
  Register #(.width(5)) register_6 (.D(WriteRegE), .en(1'b1), .Q(WriteRegM), .clk(clk), .clr(clr));
endmodule

module MEM_WB (
  input  clk,
  input  RegWriteM,
  input  MemToRegM,
  input  [31:0] aluoutM,
  input  [31:0] outputM,
  input  [4:0] WriteRegM,
  input  clr,
  output RegWriteW,
  output MemToRegW,
  output [31:0] aluoutW,
  output [31:0] outputW,
  output [4:0] WriteRegW
);

  Register #(.width(1)) register_1 (.D(RegWriteM), .en(1'b1), .Q(RegWriteW), .clk(clk), .clr(clr));
  Register #(.width(1)) register_2 (.D(MemToRegM), .en(1'b1), .Q(MemToRegW), .clk(clk), .clr(clr));
  Register #(.width(32)) register_3 (.D(aluoutM), .en(1'b1), .Q(aluoutW), .clk(clk), .clr(clr));
  Register #(.width(32)) register_4 (.D(outputM), .en(1'b1), .Q(outputW), .clk(clk), .clr(clr));
  Register #(.width(5)) register_5 (.D(WriteRegM), .en(1'b1), .Q(WriteRegW), .clk(clk));  // open: clr
endmodule

module redirect (
  input  [4:0] ID_EXE_RS,
  input  [4:0] ID_EXE_RT,
  input  [4:0] EXE_MEM_WriteReg,
  input  EXE_MEM_RegWrite,
  input  ID_EXE_ALUsrc,
  input  [4:0] MEM_WB_WriteReg,
  input  MEM_WB_RegWrite,
  output [1:0] EXE_MUX1_plus,
  output [1:0] EXE_MUX2_plus
);

  wire comparator_1_eq, comparator_2_eq, comparator_3_eq, comparator_4_eq, comparator_5_eq, comparator_6_eq,
       comparator_7_eq, comparator_8_eq, not_1_out, not_2_out, not_3_out, not_4_out;
  wire [1:0] and_1_out, and_2_out, multiplexer_1_out;

  Comparator #(.width(5)) comparator_1 (.a(EXE_MEM_WriteReg), .b({5{1'b0}}), .eq(comparator_1_eq));  // open: gt, lt
  not not_1 (not_1_out, comparator_1_eq);
  Comparator #(.width(5)) comparator_2 (.a(EXE_MEM_WriteReg), .b(ID_EXE_RS), .eq(comparator_2_eq));  // open: gt, lt
  not not_2 (not_2_out, comparator_3_eq);
  Comparator #(.width(5)) comparator_3 (.a(EXE_MEM_WriteReg), .b({5{1'b0}}), .eq(comparator_3_eq));  // open: gt, lt
  Comparator #(.width(5)) comparator_4 (.a(EXE_MEM_WriteReg), .b(ID_EXE_RT), .eq(comparator_4_eq));  // open: gt, lt
  Comparator #(.width(5)) comparator_5 (.a(MEM_WB_WriteReg), .b({5{1'b0}}), .eq(comparator_5_eq));  // open: gt, lt
  not not_3 (not_3_out, comparator_5_eq);
  Comparator #(.width(5)) comparator_6 (.a(MEM_WB_WriteReg), .b(ID_EXE_RS), .eq(comparator_6_eq));  // open: gt, lt
  Comparator #(.width(5)) comparator_7 (.a(MEM_WB_WriteReg), .b({5{1'b0}}), .eq(comparator_7_eq));  // open: gt, lt
  not not_4 (not_4_out, comparator_7_eq);
  Comparator #(.width(5)) comparator_8 (.a(MEM_WB_WriteReg), .b(ID_EXE_RT), .eq(comparator_8_eq));  // open: gt, lt
  and and_1 (and_1_out[0], EXE_MEM_RegWrite, not_1_out, comparator_2_eq);
  and and_2 (and_2_out[0], EXE_MEM_RegWrite, not_2_out, comparator_4_eq);
  and and_3 (and_1_out[1], MEM_WB_RegWrite, not_3_out, comparator_6_eq);
  and and_4 (and_2_out[1], MEM_WB_RegWrite, not_4_out, comparator_8_eq);
  Multiplexer #(.select(2), .width(2)) multiplexer_1 (
    .in0(2'b00), .in1(2'b01), .in2(2'b10), .in3(2'b01), .out(multiplexer_1_out), .sel(and_2_out));  // open: en
  Multiplexer #(.select(2), .width(2)) multiplexer_2 (
    .in0(2'b00), .in1(2'b01), .in2(2'b10), .in3(2'b01), .out(EXE_MUX2_plus), .sel(and_1_out));  // open: en
  Multiplexer #(.width(2)) multiplexer_3 (
    .in0(multiplexer_1_out), .in1(2'b11), .out(EXE_MUX1_plus), .sel(ID_EXE_ALUsrc));  // open: en
endmodule

module pause (
  input  [4:0] IF_ID_rs,
  input  [4:0] IF_ID_rt,
  input  [4:0] ID_EXE_rt,
  input  ID_EXE_MemToReg,
  output PC_we,
  output IF_ID_we,
  output ID_EXE_we
);

  wire and_1_out, comparator_1_eq, comparator_2_eq, comparator_3_eq, not_3_out, or_1_out;

  not not_1 (PC_we, and_1_out);
  not not_2 (IF_ID_we, and_1_out);
  Comparator #(.width(5)) comparator_1 (.a(ID_EXE_rt), .b({5{1'b0}}), .eq(comparator_1_eq));  // open: gt, lt
  Comparator #(.width(5)) comparator_2 (.a(ID_EXE_rt), .b(IF_ID_rt), .eq(comparator_2_eq));  // open: gt, lt
  Comparator #(.width(5)) comparator_3 (.a(ID_EXE_rt), .b(IF_ID_rs), .eq(comparator_3_eq));  // open: gt, lt
  not not_3 (not_3_out, comparator_1_eq);
  or or_1 (or_1_out, comparator_2_eq, comparator_3_eq);
  and and_1 (and_1_out, ID_EXE_MemToReg, not_3_out, or_1_out);
  not not_4 (ID_EXE_we, and_1_out);
endmodule

module beq_reANDpa (
  input  [4:0] IF_ID_rs,
  input  [4:0] IF_ID_rt,
  input  [4:0] EXE_MUXout_minus,
  input  ID_EXE_RegWrite,
  input  EXE_MEM_MemWrite,
  input  [4:0] EXE_MEM_WriteReg,
  input  EXE_MEM_RegWrite,
  output [1:0] ID_MUX1_plus,
  output [1:0] ID_MUX2_plus
);

  wire comparator_1_eq, comparator_2_eq, comparator_3_eq, comparator_4_eq, comparator_5_eq, comparator_6_eq,
       comparator_7_eq, comparator_8_eq, not_1_out, not_2_out, not_3_out, not_4_out;
  wire [1:0] and_1_out, and_2_out, multiplexer_1_out, multiplexer_3_out;

  not not_1 (not_1_out, comparator_1_eq);
  Comparator #(.width(5)) comparator_1 (.a(EXE_MUXout_minus), .b({5{1'b0}}), .eq(comparator_1_eq));  // open: gt, lt
  Comparator #(.width(5)) comparator_2 (.a(EXE_MUXout_minus), .b(IF_ID_rs), .eq(comparator_2_eq));  // open: gt, lt
  Comparator #(.width(5)) comparator_3 (.a(EXE_MUXout_minus), .b({5{1'b0}}), .eq(comparator_3_eq));  // open: gt, lt
  not not_2 (not_2_out, comparator_3_eq);
  Comparator #(.width(5)) comparator_4 (.a(EXE_MUXout_minus), .b(IF_ID_rt), .eq(comparator_4_eq));  // open: gt, lt
  not not_3 (not_3_out, comparator_5_eq);
  Comparator #(.width(5)) comparator_5 (.a(EXE_MEM_WriteReg), .b({5{1'b0}}), .eq(comparator_5_eq));  // open: gt, lt
  Comparator #(.width(5)) comparator_6 (.a(EXE_MEM_WriteReg), .b(IF_ID_rs), .eq(comparator_6_eq));  // open: gt, lt
  not not_4 (not_4_out, comparator_7_eq);
  Comparator #(.width(5)) comparator_7 (.a(EXE_MEM_WriteReg), .b({5{1'b0}}), .eq(comparator_7_eq));  // open: gt, lt
  Comparator #(.width(5)) comparator_8 (.a(EXE_MEM_WriteReg), .b(IF_ID_rt), .eq(comparator_8_eq));  // open: gt, lt
  and and_1 (and_1_out[0], ID_EXE_RegWrite, not_1_out, comparator_2_eq);
  and and_2 (and_2_out[0], ID_EXE_RegWrite, not_2_out, comparator_4_eq);
  and and_3 (and_1_out[1], EXE_MEM_RegWrite, not_3_out, comparator_6_eq);
  and and_4 (and_2_out[1], EXE_MEM_RegWrite, not_4_out, comparator_8_eq);
  Multiplexer #(.select(2), .width(2)) multiplexer_1 (
    .in0(2'b00), .in1(2'b01), .in2(2'b10), .in3(2'b01), .out(multiplexer_1_out), .sel(and_2_out));  // open: en
  Multiplexer #(.width(2)) multiplexer_2 (
    .in0(multiplexer_1_out), .in1(2'b11), .out(ID_MUX1_plus), .sel(EXE_MEM_MemWrite));  // open: en
  Multiplexer #(.select(2), .width(2)) multiplexer_3 (
    .in0(2'b00), .in1(2'b01), .in2(2'b10), .in3(2'b01), .out(multiplexer_3_out), .sel(and_1_out));  // open: en
  Multiplexer #(.width(2)) multiplexer_4 (
    .in0(multiplexer_3_out), .in1(2'b11), .out(ID_MUX2_plus), .sel(EXE_MEM_MemWrite));  // open: en
endmodule
