// Logisim project rf.circ as structural Verilog: 1 circuit, main circuit main
module main (
  input  [7:0] rd,
  input  [2:0] ra,
  input  [2:0] rb,
  input  we,
  input  [2:0] rw,
  output [7:0] out_6,
  output [7:0] out_7
);

  wire and_1_out, and_2_out, and_3_out, and_4_out, and_5_out, and_6_out, and_7_out, and_8_out, clk_out,
       decoder_1_out0, decoder_1_out1, decoder_1_out2, decoder_1_out3, decoder_1_out4, decoder_1_out5,
       decoder_1_out6, decoder_1_out7;
  wire [7:0] register_1_q, register_2_q, register_3_q, register_4_q, register_5_q, register_6_q,
       register_7_q, register_8_q;

  Decoder #(.select(3), .enable("false")) decoder_1 (
    .out0(decoder_1_out0), .out1(decoder_1_out1), .out2(decoder_1_out2), .out3(decoder_1_out3),
    .out4(decoder_1_out4), .out5(decoder_1_out5), .out6(decoder_1_out6), .out7(decoder_1_out7), .sel(rw));
  and and_1 (and_1_out, decoder_1_out0, we);
  and and_2 (and_2_out, decoder_1_out1, we);
  and and_3 (and_3_out, decoder_1_out2, we);
  and and_4 (and_4_out, decoder_1_out3, we);
  and and_5 (and_5_out, decoder_1_out4, we);
  and and_6 (and_6_out, decoder_1_out5, we);
  and and_7 (and_7_out, decoder_1_out6, we);
  and and_8 (and_8_out, decoder_1_out7, we);
  Clock clk (.out(clk_out));
  Register register_1 (.D(rd), .en(and_1_out), .Q(register_1_q), .clk(clk_out));  // open: clr
  Register register_2 (.D(rd), .en(and_5_out), .Q(register_2_q), .clk(clk_out));  // open: clr
  Register register_3 (.D(rd), .en(and_2_out), .Q(register_3_q), .clk(clk_out));  // open: clr
  Register register_4 (.D(rd), .en(and_6_out), .Q(register_4_q), .clk(clk_out));  // open: clr
  Register register_5 (.D(rd), .en(and_3_out), .Q(register_5_q), .clk(clk_out));  // open: clr
  Register register_6 (.D(rd), .en(and_7_out), .Q(register_6_q), .clk(clk_out));  // open: clr
  Multiplexer #(.select(3), .width(8)) multiplexer_1 (
    .in0(register_1_q), .in1(register_3_q), .in2(register_5_q), .in3(register_7_q), .in4(register_2_q),
    .in5(register_4_q), .in6(register_6_q), .in7(register_8_q), .out(out_6), .sel(ra));  // open: en
  Register register_7 (.D(rd), .en(and_4_out), .Q(register_7_q), .clk(clk_out));  // open: clr
  Register register_8 (.D(rd), .en(and_8_out), .Q(register_8_q), .clk(clk_out));  // open: clr
  Multiplexer #(.select(3), .width(8)) multiplexer_2 (
    .in0(register_1_q), .in1(register_3_q), .in2(register_5_q), .in3(register_7_q), .in4(register_2_q),
    .in5(register_4_q), .in6(register_6_q), .in7(register_8_q), .out(out_7), .sel(rb));  // open: en
endmodule
